# Fritzing sketch curcuitSchema (saved by Fritzing 0.9.3b)
circuit board: 8.46667cm x 5.64444cm
breadboards: 1

parts:
  U1 = ESP32-38PinWide [part_number=ESP32-38PinWide]
  IR1 = TSOP312.., 314.. [package=THT]
  LED1 = Infrared LED - 5mm [package="5 mm [THT]"]
  R1 = Resistor [tolerance=±5% resistance=33 package="0402 [SMD]"]

nets:
  N1: U1.VIN, IR1.Vs
  N2: U1.GPIO15, IR1.Data
  N3: U1.GPIO5, R1.Pin_0
  GND: U1.GND, IR1.GND, LED1.cathode
  N4: LED1.anode, R1.Pin_1

custom parts:
  ESP32-38PinWide: Generic 38-Pin ESP32 with wide format (only access to one side of pins on a breadboard) based on Stephen Lilley's HiLetgo ESP-WROOM-32 ESP32 ESP-32S Development Board.
  Infrared LED - 5mm: A generic infrared LED (~1.2V)
